// Logisim project BIP2.1.circ as structural Verilog: 9 circuits, main circuit main
module main (
);

  wire clock_out, controle_1_en_pc, controle_1_en_ram, controle_1_sel_op2, controle_1_ula_demux2,
       controle_1_wr_acc, controle_1_wr_ram, LIMPA_RAM_out, RESET_out;
  wire [1:0] controle_1_sel_op1;
  wire [15:0] ACC_q, adder_1_out, adder_2_out, and_1_out, and_2_out, and_3_out, demultiplexer_1_out0,
       demultiplexer_1_out1, demultiplexer_2_out0, demultiplexer_2_out1, IR_q, multiplexer_1_out,
       multiplexer_2_out, multiplexer_3_out, PC_q, ram_1_data, rom_1_data, subtractor_1_out;

  Clock clock (.out(clock_out));
  assign and_1_out = PC_q & 16'hfff;  // AND_Gate and_1, 16 bits wide
  Adder #(.width(16)) adder_1 (.a(and_1_out), .b(16'h1), .out(adder_1_out));  // open: cin, cout
  Button RESET (.out(RESET_out));
  Button LIMPA_RAM (.out(LIMPA_RAM_out));
  Register #(.width(16)) PC (.D(adder_1_out), .en(controle_1_en_pc), .Q(PC_q), .clk(clock_out), .clr(RESET_out));
  RAM #(.addrWidth(16), .dataWidth(16), .bus("separate")) ram_1 (
    .addr(and_2_out), .din(ACC_q), .data(ram_1_data), .str(controle_1_wr_ram), .sel(controle_1_en_ram),
    .clk(clock_out), .clr(LIMPA_RAM_out));  // open: ld
  ROM #(.addrWidth(16), .dataWidth(16)) rom_1 (.addr(PC_q), .data(rom_1_data), .sel(1'b1));
  Multiplexer #(.width(16), .enable("false")) multiplexer_1 (
    .in0(ram_1_data), .in1(and_2_out), .out(multiplexer_1_out), .sel(controle_1_sel_op2));
  Demultiplexer #(.width(16), .enable("false")) demultiplexer_1 (
    .out0(demultiplexer_1_out0), .out1(demultiplexer_1_out1), .in(multiplexer_1_out),
    .sel(controle_1_ula_demux2));
  assign and_2_out = 16'hfff & IR_q;  // AND_Gate and_2, 16 bits wide
  Register #(.width(16)) IR (.D(rom_1_data), .en(1'b1), .Q(IR_q), .clk(clock_out), .clr(RESET_out));
  Multiplexer #(.select(2), .width(16), .enable("false")) multiplexer_2 (
    .in0(ram_1_data), .in1(and_2_out), .in2(multiplexer_3_out), .out(multiplexer_2_out),
    .sel(controle_1_sel_op1));  // open: in3
  Adder #(.width(16)) adder_2 (
    .a(demultiplexer_2_out0), .b(demultiplexer_1_out0), .out(adder_2_out));  // open: cin, cout
  Register #(.width(16)) ACC (
    .D(multiplexer_2_out), .en(controle_1_wr_acc), .Q(ACC_q), .clk(clock_out), .clr(RESET_out));
  assign and_3_out = IR_q & 16'hf000;  // AND_Gate and_3, 16 bits wide
  Demultiplexer #(.width(16), .enable("false")) demultiplexer_2 (
    .out0(demultiplexer_2_out0), .out1(demultiplexer_2_out1), .in(ACC_q), .sel(controle_1_ula_demux2));
  Subtractor #(.width(16)) subtractor_1 (
    .a(demultiplexer_2_out1), .b(demultiplexer_1_out1), .out(subtractor_1_out));  // open: bin, bout
  Multiplexer #(.width(16), .enable("false")) multiplexer_3 (
    .in0(adder_2_out), .in1(subtractor_1_out), .out(multiplexer_3_out), .sel(controle_1_ula_demux2));
  CONTROLE controle_1 (
    .WR_RAM(controle_1_wr_ram), .EN_RAM(controle_1_en_ram), .WR_ACC(controle_1_wr_acc),
    .SEL_OP1(controle_1_sel_op1), .SEL_OP2(controle_1_sel_op2), .ULA_DEMUX2(controle_1_ula_demux2),
    .EN_PC(controle_1_en_pc), .in_1(and_3_out));

  // Notes on the sheet:
  //   contents of rom_1 (hex, n*v repeats v):
  //   2000 4001 7001 1002 5002 1003
endmodule

module EN_RAM (
  input  [15:0] in_1,
  output out_2
);

  wire comparator_1_eq, comparator_2_eq, comparator_3_eq, comparator_4_eq;

  Comparator #(.width(16)) comparator_1 (.a(in_1), .b(16'h1000), .eq(comparator_1_eq));  // open: gt, lt
  Comparator #(.width(16)) comparator_2 (.a(in_1), .b(16'h2000), .eq(comparator_2_eq));  // open: gt, lt
  Comparator #(.width(16)) comparator_3 (.a(in_1), .b(16'h4000), .eq(comparator_3_eq));  // open: gt, lt
  Comparator #(.width(16)) comparator_4 (.a(in_1), .b(16'h6000), .eq(comparator_4_eq));  // open: gt, lt
  or or_1 (out_2, comparator_1_eq, comparator_2_eq, comparator_3_eq, comparator_4_eq);
endmodule

module WR_RAM (
  input  [15:0] in_1,
  output EN_RAM
);

  Comparator #(.width(16)) comparator_1 (.a(in_1), .b(16'h1000), .eq(EN_RAM));  // open: gt, lt
endmodule

module CONTROLE (
  input  [15:0] in_1,
  output WR_RAM,
  output EN_RAM,
  output WR_ACC,
  output [1:0] SEL_OP1,
  output SEL_OP2,
  output ULA_DEMUX2,
  output EN_PC
);

  WR_RAM wr_ram_1 (.in_1(in_1), .EN_RAM(WR_RAM));
  EN_RAM en_ram_1 (.in_1(in_1), .out_2(EN_RAM));
  WR_ACC wr_acc_1 (.in_1(in_1), .out_2(WR_ACC));
  SEL_OP1 sel_op1_1 (.in_1(in_1), .out_2(SEL_OP1));
  SEL_OP2 sel_op2_1 (.in_1(in_1), .out_2(SEL_OP2));
  ULA_demux2 ula_demux2_1 (.in_1(in_1), .out_2(ULA_DEMUX2));
  EN_PC en_pc_1 (.in_1(in_1), .EN_PC(EN_PC));
endmodule

module WR_ACC (
  input  [15:0] in_1,
  output out_2
);

  wire comparator_1_eq, comparator_2_eq, comparator_3_eq, comparator_4_eq, comparator_5_eq, comparator_6_eq;

  Comparator #(.width(16)) comparator_1 (.a(in_1), .b(16'h2000), .eq(comparator_1_eq));  // open: gt, lt
  Comparator #(.width(16)) comparator_2 (.a(in_1), .b(16'h3000), .eq(comparator_2_eq));  // open: gt, lt
  Comparator #(.width(16)) comparator_3 (.a(in_1), .b(16'h4000), .eq(comparator_3_eq));  // open: gt, lt
  Comparator #(.width(16)) comparator_4 (.a(in_1), .b(16'h5000), .eq(comparator_4_eq));  // open: gt, lt
  Comparator #(.width(16)) comparator_5 (.a(in_1), .b(16'h6000), .eq(comparator_5_eq));  // open: gt, lt
  Comparator #(.width(16)) comparator_6 (.a(in_1), .b(16'h7000), .eq(comparator_6_eq));  // open: gt, lt
  or or_1 (out_2, comparator_1_eq, comparator_2_eq, comparator_3_eq, comparator_4_eq, comparator_5_eq, comparator_6_eq);
endmodule

module SEL_OP1 (
  input  [15:0] in_1,
  output [1:0] out_2
);

  wire comparator_1_eq, comparator_2_eq, comparator_3_eq, comparator_4_eq, comparator_5_eq, or_1_out;

  Comparator #(.width(16)) comparator_1 (.a(in_1), .b(16'h4000), .eq(comparator_1_eq));  // open: gt, lt
  Comparator #(.width(16)) comparator_2 (.a(in_1), .b(16'h5000), .eq(comparator_2_eq));  // open: gt, lt
  Comparator #(.width(16)) comparator_3 (.a(in_1), .b(16'h6000), .eq(comparator_3_eq));  // open: gt, lt
  Comparator #(.width(16)) comparator_4 (.a(in_1), .b(16'h7000), .eq(comparator_4_eq));  // open: gt, lt
  Comparator #(.width(16)) comparator_5 (.a(in_1), .b(16'h3000), .eq(comparator_5_eq));  // open: gt, lt
  or or_1 (or_1_out, comparator_1_eq, comparator_2_eq, comparator_3_eq, comparator_4_eq);
  assign out_2 = {{1{or_1_out}}, comparator_5_eq};  // Bit_Extender bit_extender_1
endmodule

// ULA/DEMUX2
module ULA_demux2 (
  input  [15:0] in_1,
  output out_2
);

  wire comparator_1_eq, comparator_2_eq;

  Comparator #(.width(16)) comparator_1 (.a(in_1), .b(16'h6000), .eq(comparator_1_eq));  // open: gt, lt
  Comparator #(.width(16)) comparator_2 (.a(in_1), .b(16'h7000), .eq(comparator_2_eq));  // open: gt, lt
  or or_1 (out_2, comparator_1_eq, comparator_2_eq);
endmodule

module SEL_OP2 (
  input  [15:0] in_1,
  output out_2
);

  wire comparator_1_eq, comparator_2_eq, comparator_3_eq;

  Comparator #(.width(16)) comparator_1 (.a(in_1), .b(16'h3000), .eq(comparator_1_eq));  // open: gt, lt
  Comparator #(.width(16)) comparator_2 (.a(in_1), .b(16'h5000), .eq(comparator_2_eq));  // open: gt, lt
  Comparator #(.width(16)) comparator_3 (.a(in_1), .b(16'h7000), .eq(comparator_3_eq));  // open: gt, lt
  or or_1 (out_2, comparator_1_eq, comparator_2_eq, comparator_3_eq);
endmodule

module EN_PC (
  input  [15:0] in_1,
  output EN_PC
);

  wire comparator_1_eq;

  Comparator #(.width(16)) comparator_1 (.a(in_1), .b({16{1'b0}}), .eq(comparator_1_eq));  // open: gt, lt
  not not_1 (EN_PC, comparator_1_eq);
endmodule
