// Logisim project cc.circ as structural Verilog: 2 circuits, main circuit main
module main (
  input  [15:0] DOUT_ROM,
  input  CLOCK,
  input  RESET,
  input  [15:0] DOUT_RAM,
  input  [1:0] SEL_OP1,
  input  SEL_OP2,
  input  WR_ACC,
  input  Sel_ULA,
  output [11:0] ADD_RAM,
  output [3:0] OPCODE,
  output [15:0] DIN_RAM
);

  wire [15:0] bit_extender_1_out, multiplexer_1_out, multiplexer_2_out, ula_1_out_ua;

  Multiplexer #(.width(16), .enable("false")) multiplexer_1 (
    .in0(DOUT_RAM), .in1(bit_extender_1_out), .out(multiplexer_1_out), .sel(SEL_OP2));
  Register #(.width(16)) IR (.D(DOUT_ROM), .en(1'b1), .Q({OPCODE, ADD_RAM}), .clk(CLOCK), .clr(RESET));
  assign bit_extender_1_out = {{4{ADD_RAM[11]}}, ADD_RAM};  // Bit_Extender bit_extender_1
  Multiplexer #(.select(2), .width(16), .enable("false")) multiplexer_2 (
    .in0(DOUT_RAM), .in1(bit_extender_1_out), .in2(ula_1_out_ua), .in3({16{1'b0}}), .out(multiplexer_2_out),
    .sel(SEL_OP1));
  Register #(.width(16)) ACC (.D(multiplexer_2_out), .en(WR_ACC), .Q(DIN_RAM), .clk(CLOCK), .clr(RESET));
  ULA ula_1 (.Data_A(multiplexer_1_out), .Data_B(DIN_RAM), .Sel_ULA(Sel_ULA), .out_UA(ula_1_out_ua));
endmodule

module ULA (
  input  [15:0] Data_A,
  input  [15:0] Data_B,
  input  Sel_ULA,
  output [15:0] out_UA
);

  wire [15:0] adder_1_out, subtractor_1_out;

  Adder #(.width(16)) adder_1 (.a(Data_B), .b(Data_A), .out(adder_1_out));  // open: cin, cout
  Multiplexer #(.width(16), .enable("false")) multiplexer_1 (
    .in0(subtractor_1_out), .in1(adder_1_out), .out(out_UA), .sel(Sel_ULA));
  Subtractor #(.width(16)) subtractor_1 (.a(Data_A), .b(Data_B), .out(subtractor_1_out));  // open: bin, bout
endmodule
